// Logisim project Cache.circ as structural Verilog: 7 circuits, main circuit implementation
module implementation (
  input  [9:0] CpuAddressIn,
  input  CpuReadIn,
  input  CpuWriteIn,
  input  [7:0] CpuWriteValueIn,
  input  [31:0] LineFromMemIn,
  input  ClkIn,
  output ReadyOut,
  output DidContainOut,
  output [7:0] ByteReadOut,
  output [7:0] MemAddressOut,
  output MemReadOut,
  output MemWriteOut,
  output [31:0] Line2MemOut
);

  wire checkDidContain, Contains0, Contains1, didContain_t, Dirty, Dirty0, Dirty1, init, updateAge;
  wire [2:0] nextstate_1_st2_next, register_3_q;
  wire [4:0] signalS0, signalS1;
  wire [7:0] ByteReadS0, ByteReadS1;
  wire [9:0] CpuAddressIn_t;
  wire [31:0] Line2Mem0, Line2Mem1;

  Register #(.width(1)) register_1 (
    .D(didContain_t), .en(checkDidContain), .clk(ClkIn), .Q(DidContainOut));  // open: clr
  Demultiplexer #(.enable("false"), .width(5)) demultiplexer_1 (
    .out0(signalS0), .out1(signalS1), .in({1'b1, didContain_t, updateAge, MemWriteOut, MemReadOut}),
    .sel(CpuAddressIn[2]));
  Register #(.width(20)) register_2 (
    .D({CpuAddressIn_t, CpuReadIn, CpuWriteIn, CpuWriteValueIn}), .en(ReadyOut), .clk(ClkIn),
    .Q({CpuAddressIn, CpuReadIn, CpuWriteIn, CpuWriteValueIn}));  // open: clr
  nextState nextstate_1 (
    .St2(register_3_q[0]), .St1(register_3_q[1]), .St0(register_3_q[2]), .CPU_Read(CpuReadIn),
    .CPU_Write(CpuWriteIn), .dirty(Dirty), .didContain(didContain_t), .St2_next(nextstate_1_st2_next[0]),
    .St1_next(nextstate_1_st2_next[1]), .St0_next(nextstate_1_st2_next[2]));
  Set Set0 (
    .CpuAddressIn(CpuAddressIn), .ClkIn(ClkIn), .CpuReadIn(CpuReadIn), .CpuWriteIn(CpuWriteIn),
    .CpuWriteValueIn(CpuWriteValueIn), .LineFromMemIn(LineFromMemIn), .MemoryRead(signalS0[0]),
    .MemoryWrite(signalS0[1]), .updateAges(signalS0[2]), .didContain(signalS0[3]), .signals(signalS0[4]),
    .init(init), .ByteRead(ByteReadS0), .Contains(Contains0), .Line2Mem(Line2Mem0), .memAdd(MemAddressOut),
    .dirty(Dirty0));
  Set Set1 (
    .CpuAddressIn(CpuAddressIn), .ClkIn(ClkIn), .CpuReadIn(CpuReadIn), .CpuWriteIn(CpuWriteIn),
    .CpuWriteValueIn(CpuWriteValueIn), .LineFromMemIn(LineFromMemIn), .MemoryRead(signalS1[0]),
    .MemoryWrite(signalS1[1]), .updateAges(signalS1[2]), .didContain(signalS1[3]), .signals(signalS1[4]),
    .init(init), .ByteRead(ByteReadS1), .Contains(Contains1), .Line2Mem(Line2Mem1), .memAdd(MemAddressOut),
    .dirty(Dirty1));
  Register #(.width(3)) register_3 (.D(nextstate_1_st2_next), .clk(ClkIn), .Q(register_3_q));  // open: en, clr
  Multiplexer #(.enable("false"), .width(8)) multiplexer_1 (
    .in0(ByteReadS0), .in1(ByteReadS1), .out(ByteReadOut), .sel(CpuAddressIn[2]));
  Multiplexer #(.enable("false")) multiplexer_2 (
    .in0(Contains0), .in1(Contains1), .out(didContain_t), .sel(CpuAddressIn[2]));
  Multiplexer #(.enable("false"), .width(32)) multiplexer_3 (
    .in0(Line2Mem0), .in1(Line2Mem1), .out(Line2MemOut), .sel(CpuAddressIn[2]));
  Multiplexer #(.enable("false")) multiplexer_4 (.in0(Dirty0), .in1(Dirty1), .out(Dirty), .sel(CpuAddressIn[2]));
  getoutput getoutput_1 (
    .St2(register_3_q[0]), .St1(register_3_q[1]), .St0(register_3_q[2]), .init(init), .ready(ReadyOut),
    .mem_Read(MemReadOut), .mem_Write(MemWriteOut), .update_Age(updateAge), .ch_DidContain(checkDidContain));

  // Other names for the same wires on the sheet: MemRead = MemReadOut; MemWrite = MemWriteOut;
  //   CpuWriteValue[7:0] = CpuWriteValueIn; CpuWrite = CpuWriteIn; CpuRead = CpuReadIn;
  //   CpuAddress[9:0] = CpuAddressIn; offsetBits[1:0] = CpuAddressIn[1:0]; setBits = CpuAddressIn[2];
  //   tagBits[6:0] = CpuAddressIn[9:3]; clk = ClkIn; DidContain = DidContainOut; LineFromMem[31:0] = LineFromMemIn;
  //   MemAddress[7:0] = MemAddressOut; Ready = ReadyOut; ByteRead[7:0] = ByteReadOut;
  //   SelectedSetByteRead[7:0] = ByteReadOut; Line2Mem[31:0] = Line2MemOut; SelectedSetLine2Mem[31:0] = Line2MemOut

  // Notes on the sheet:
  //   Cache project
  //   Done By Muskan Kumar
  //   Student ID: 917494628
endmodule

module Set (
  input  [9:0] CpuAddressIn,
  input  ClkIn,
  input  CpuReadIn,
  input  CpuWriteIn,
  input  [7:0] CpuWriteValueIn,
  input  [31:0] LineFromMemIn,
  input  MemoryRead,
  input  MemoryWrite,
  input  updateAges,
  input  didContain,
  input  signals,
  input  init,
  output [7:0] ByteRead,
  output Contains,
  output [31:0] Line2Mem,
  output [7:0] memAdd,
  output dirty
);

  wire contains0, contains1, contains2, CpuWrite0, CpuWrite1, CpuWrite2, didContain0, didContain1,
       didContain2, Dirty0, Dirty1, Dirty2, MemoryRead0, MemoryRead1, MemoryRead2;
  wire [1:0] Age0, Age1, Age2, index, last_Used, multiplexer_2_out, multiplexer_3_out, multiplexer_4_out,
       newAge0, newAge1, newAge2, oldWay;
  wire [7:0] ByteRead0, ByteRead1, ByteRead2;
  wire [31:0] Line2Mem0, Line2Mem1, Line2Mem2;

  Demultiplexer #(.enable("false"), .select(2)) demultiplexer_1 (
    .out0(MemoryRead0), .out1(MemoryRead1), .out2(MemoryRead2), .in(MemoryRead), .sel(last_Used));  // open: out3
  Multiplexer #(.enable("false"), .width(2)) multiplexer_1 (
    .in0(oldWay), .in1(index), .out(last_Used), .sel(didContain));
  Demultiplexer #(.enable("false"), .select(2)) demultiplexer_2 (
    .out0(didContain0), .out1(didContain1), .out2(didContain2), .in(didContain), .sel(last_Used));  // open: out3
  Demultiplexer #(.enable("false"), .select(2)) demultiplexer_3 (
    .out0(CpuWrite0), .out1(CpuWrite1), .out2(CpuWrite2), .in(CpuWriteIn), .sel(last_Used));  // open: out3
  getOldway getoldway_1 (.age0(Age0), .age1(Age1), .age2(Age2), .oldest_Way(oldWay));
  Multiplexer #(.enable("false"), .width(2)) multiplexer_2 (
    .in0(newAge0), .in1(2'b00), .out(multiplexer_2_out), .sel(init));
  Multiplexer #(.enable("false"), .width(2)) multiplexer_3 (
    .in0(newAge1), .in1(2'b01), .out(multiplexer_3_out), .sel(init));
  Multiplexer #(.enable("false"), .width(2)) multiplexer_4 (
    .in0(newAge2), .in1(2'b10), .out(multiplexer_4_out), .sel(init));
  newAge newage_1 (
    .age_0(Age0), .age_1(Age1), .age_2(Age2), .last_used(last_Used), .init(init), .newAge_0(newAge0),
    .newAge_1(newAge1), .newAge_2(newAge2));
  Way Way_0 (
    .CpuAddressIn(CpuAddressIn), .ClkIn(ClkIn), .LineFromMemIn(LineFromMemIn), .updateAge(updateAges),
    .newAge(multiplexer_2_out), .didContain(didContain0), .MemoryRead(MemoryRead0), .CpuWriteIn(CpuWrite0),
    .CpuWriteValueIn(CpuWriteValueIn), .init(init), .CpuReadIn(CpuReadIn), .Contains(contains0),
    .ByteRead(ByteRead0), .AgeOut(Age0), .Line2MemE(Line2Mem0), .Dirty(Dirty0));
  Way Way_1 (
    .CpuAddressIn(CpuAddressIn), .ClkIn(ClkIn), .LineFromMemIn(LineFromMemIn), .updateAge(updateAges),
    .newAge(multiplexer_3_out), .didContain(didContain1), .MemoryRead(MemoryRead1), .CpuWriteIn(CpuWrite1),
    .CpuWriteValueIn(CpuWriteValueIn), .init(init), .CpuReadIn(CpuReadIn), .Contains(contains1),
    .ByteRead(ByteRead1), .AgeOut(Age1), .Line2MemE(Line2Mem1), .Dirty(Dirty1));
  Way Way_2 (
    .CpuAddressIn(CpuAddressIn), .ClkIn(ClkIn), .LineFromMemIn(LineFromMemIn), .updateAge(updateAges),
    .newAge(multiplexer_4_out), .didContain(didContain2), .MemoryRead(MemoryRead2), .CpuWriteIn(CpuWrite2),
    .CpuWriteValueIn(CpuWriteValueIn), .init(init), .CpuReadIn(CpuReadIn), .Contains(contains2),
    .ByteRead(ByteRead2), .AgeOut(Age2), .Line2MemE(Line2Mem2), .Dirty(Dirty2));
  Multiplexer #(.enable("false"), .select(2), .width(32)) multiplexer_5 (
    .in0(Line2Mem0), .in1(Line2Mem1), .in2(Line2Mem2), .out(Line2Mem), .sel(index));  // open: in3
  Multiplexer #(.enable("false"), .select(2)) multiplexer_6 (
    .in0(Dirty0), .in1(Dirty1), .in2(Dirty2), .out(dirty), .sel(index));  // open: in3
  Multiplexer #(.enable("false"), .select(2), .width(8)) multiplexer_7 (
    .in0(ByteRead0), .in1(ByteRead1), .in2(ByteRead2), .out(ByteRead), .sel(index));  // open: in3
  BitFinder #(.width(3)) bitfinder_1 (.in({contains2, contains1, contains0}), .index(index), .found(Contains));

  assign memAdd = CpuAddressIn[9:2];

  // Other names for the same wires on the sheet: clk = ClkIn; CpuAddress[9:0] = CpuAddressIn; CpuRead = CpuReadIn;
  //   CpuWrite = CpuWriteIn; CpuWriteValue[7:0] = CpuWriteValueIn; LineFromMem[31:0] = LineFromMemIn;
  //   memAddress[7:0] = CpuAddressIn[9:2]
endmodule

module Way (
  input  [9:0] CpuAddressIn,
  input  ClkIn,
  input  [31:0] LineFromMemIn,
  input  updateAge,
  input  [1:0] newAge,
  input  didContain,
  input  MemoryRead,
  input  CpuWriteIn,
  input  [7:0] CpuWriteValueIn,
  input  init,
  input  CpuReadIn,
  output Contains,
  output [7:0] ByteRead,
  output [1:0] AgeOut,
  output [31:0] Line2MemE,
  output Dirty
);

  wire comparator_1_eq, CpuWrite0, CpuWrite1, CpuWrite2, CpuWrite3, multiplexer_1_out, multiplexer_3_out,
       or_1_out, or_2_out, or_3_out, or_4_out, or_5_out, Valid;
  wire [6:0] register_1_q;
  wire [7:0] B0, B1, B2, B3;

  Multiplexer #(.enable("false")) multiplexer_1 (.in0(1'b1), .in1(1'b0), .out(multiplexer_1_out), .sel(MemoryRead));
  or or_1 (or_1_out, MemoryRead, CpuWriteIn);
  Register #(.width(7)) register_1 (
    .D(CpuAddressIn[9:3]), .en(MemoryRead), .clk(ClkIn), .Q(register_1_q));  // open: clr
  Register #(.width(1)) register_2 (.D(multiplexer_1_out), .en(or_1_out), .clk(ClkIn), .Q(Dirty));  // open: clr
  Register #(.width(1)) register_3 (.D(1'b1), .en(MemoryRead), .clk(ClkIn), .Q(Valid));  // open: clr
  Comparator #(.width(7)) comparator_1 (.a(CpuAddressIn[9:3]), .b(register_1_q), .eq(comparator_1_eq));  // open: gt, lt
  and and_1 (Contains, comparator_1_eq, Valid);
  Demultiplexer #(.enable("false"), .select(2)) demultiplexer_1 (
    .out0(CpuWrite0), .out1(CpuWrite1), .out2(CpuWrite2), .out3(CpuWrite3), .in(CpuWriteIn),
    .sel(CpuAddressIn[1:0]));
  or or_2 (or_2_out, CpuWrite0, MemoryRead);
  or or_3 (or_3_out, CpuWrite1, MemoryRead);
  or or_4 (or_4_out, CpuWrite2, MemoryRead);
  or or_5 (or_5_out, CpuWrite3, MemoryRead);
  Register register_4 (.D(LineFromMemIn[7:0]), .en(or_2_out), .clk(ClkIn), .Q(B0));  // open: clr
  Register register_5 (.D(LineFromMemIn[15:8]), .en(or_3_out), .clk(ClkIn), .Q(B1));  // open: clr
  Register register_6 (.D(LineFromMemIn[23:16]), .en(or_4_out), .clk(ClkIn), .Q(B2));  // open: clr
  Register register_7 (.D(LineFromMemIn[31:24]), .en(or_5_out), .clk(ClkIn), .Q(B3));  // open: clr
  Multiplexer #(.enable("false"), .select(2), .width(8)) multiplexer_2 (
    .in0(B0), .in1(B1), .in2(B2), .in3(B3), .out(ByteRead), .sel(CpuAddressIn[1:0]));
  Multiplexer #(.enable("false")) multiplexer_3 (.in0(updateAge), .in1(1'b1), .out(multiplexer_3_out), .sel(init));
  Register #(.width(2)) register_8 (.D(newAge), .en(multiplexer_3_out), .clk(ClkIn), .Q(AgeOut));  // open: clr

  assign Line2MemE = LineFromMemIn;

  // Other names for the same wires on the sheet: Age[1:0] = AgeOut; clk = ClkIn; CpuAddress[9:0] = CpuAddressIn;
  //   Offset[1:0] = CpuAddressIn[1:0]; Set = CpuAddressIn[2]; Tag[6:0] = CpuAddressIn[9:3]; CpuRead = CpuReadIn;
  //   CpuWrite = CpuWriteIn; CpuWriteValue[7:0] = CpuWriteValueIn; Byte0[7:0] = LineFromMemIn[7:0];
  //   LineFromMem[31:0] = LineFromMemIn; Byte1[7:0] = LineFromMemIn[15:8]; Byte2[7:0] = LineFromMemIn[23:16];
  //   Byte3[7:0] = LineFromMemIn[31:24]
endmodule

module getOldway (
  input  [1:0] age0,
  input  [1:0] age1,
  input  [1:0] age2,
  output [1:0] oldest_Way
);

  wire comparator_1_gt, comparator_1_lt, comparator_2_gt, comparator_3_gt;
  wire [2:0] and_1_out;

  Comparator #(.mode("unsigned"), .width(2)) comparator_1 (
    .a(age0), .b(age1), .gt(comparator_1_gt), .lt(comparator_1_lt));  // open: eq
  Comparator #(.mode("unsigned"), .width(2)) comparator_2 (
    .a(age0), .b(age2), .gt(comparator_2_gt), .lt(and_1_out[2]));  // open: eq
  Comparator #(.mode("unsigned"), .width(2)) comparator_3 (.a(age1), .b(age2), .gt(comparator_3_gt));  // open: eq, lt
  and and_1 (and_1_out[0], comparator_1_gt, comparator_2_gt);
  and and_2 (and_1_out[1], comparator_1_lt, comparator_3_gt);
  BitFinder #(.width(3)) bitfinder_1 (.in(and_1_out), .index(oldest_Way));  // open: found
endmodule

module newAge (
  input  [1:0] age_0,
  input  [1:0] age_1,
  input  [1:0] age_2,
  input  [1:0] last_used,
  input  init,
  output [1:0] newAge_0,
  output [1:0] newAge_1,
  output [1:0] newAge_2
);

  wire [1:0] adder_1_out, adder_2_out, adder_3_out, multiplexer_1_out, multiplexer_3_out, multiplexer_4_out;
  wire [2:0] comparator_1_gt, comparator_2_gt, comparator_3_gt;

  Comparator #(.mode("unsigned"), .width(2)) comparator_1 (
    .a(age_0), .b(last_used), .gt(comparator_1_gt[0]), .eq(comparator_1_gt[1]), .lt(comparator_1_gt[2]));
  Adder #(.width(2)) adder_1 (.a(age_0), .b(2'b01), .out(adder_1_out));  // open: cin, cout
  Adder #(.width(2)) adder_2 (.a(age_1), .b(2'b01), .out(adder_2_out));  // open: cin, cout
  Adder #(.width(2)) adder_3 (.a(age_2), .b(2'b01), .out(adder_3_out));  // open: cin, cout
  Multiplexer #(.enable("false"), .select(3), .width(2)) multiplexer_1 (
    .in1(age_0), .in2(2'b00), .in3(2'b00), .in4(adder_1_out), .in5(2'b00), .in6(2'b00), .in7(2'b00),
    .out(multiplexer_1_out), .sel(comparator_1_gt));  // open: in0
  Comparator #(.mode("unsigned"), .width(2)) comparator_2 (
    .a(age_1), .b(last_used), .gt(comparator_2_gt[0]), .eq(comparator_2_gt[1]), .lt(comparator_2_gt[2]));
  Comparator #(.mode("unsigned"), .width(2)) comparator_3 (
    .a(age_2), .b(last_used), .gt(comparator_3_gt[0]), .eq(comparator_3_gt[1]), .lt(comparator_3_gt[2]));
  Multiplexer #(.enable("false"), .width(2)) multiplexer_2 (
    .in0(multiplexer_1_out), .in1(2'b00), .out(newAge_0), .sel(init));
  Multiplexer #(.enable("false"), .select(3), .width(2)) multiplexer_3 (
    .in1(age_1), .in2(2'b00), .in3(2'b00), .in4(adder_2_out), .in5(2'b00), .in6(2'b00), .in7(2'b00),
    .out(multiplexer_3_out), .sel(comparator_2_gt));  // open: in0
  Multiplexer #(.enable("false"), .select(3), .width(2)) multiplexer_4 (
    .in1(age_2), .in2(2'b00), .in3(2'b00), .in4(adder_3_out), .in5(2'b00), .in6(2'b00), .in7(2'b00),
    .out(multiplexer_4_out), .sel(comparator_3_gt));  // open: in0
  Multiplexer #(.enable("false"), .width(2)) multiplexer_5 (
    .in0(multiplexer_3_out), .in1(2'b01), .out(newAge_1), .sel(init));
  Multiplexer #(.enable("false"), .width(2)) multiplexer_6 (
    .in0(multiplexer_4_out), .in1(2'b10), .out(newAge_2), .sel(init));

  // Other names for the same wires on the sheet: age0[1:0] = age_0; age1[1:0] = age_1; age2[1:0] = age_2
endmodule

module nextState (
  input  St2,
  input  St1,
  input  St0,
  input  CPU_Read,
  input  CPU_Write,
  input  dirty,
  input  didContain,
  output St2_next,
  output St1_next,
  output St0_next
);

  wire and_1_out, and_2_out, and_3_out, and_4_out, and_5_out, and_6_out, and_7_out, and_8_out, and_9_out,
       and_10_out, and_11_out, and_12_out, not_1_out, not_2_out, not_3_out, not_4_out, not_5_out;

  not not_1 (not_1_out, St2);
  not not_2 (not_2_out, St1);
  not not_3 (not_3_out, St0);
  not not_4 (not_4_out, CPU_Read);
  not not_5 (not_5_out, didContain);
  and and_1 (and_1_out, not_1_out, St1, not_3_out, not_5_out);
  and and_2 (and_2_out, not_1_out, St1, St0, not_4_out);
  and and_3 (and_3_out, St2, not_2_out, St0);
  and and_4 (and_4_out, not_1_out, not_2_out, St0);
  and and_5 (and_5_out, not_1_out, St0, not_4_out);
  and and_6 (and_6_out, not_1_out, St1, not_3_out, didContain);
  and and_7 (and_7_out, St2, not_2_out, not_3_out);
  and and_8 (and_8_out, not_2_out, not_3_out);
  and and_9 (and_9_out, not_3_out, didContain);
  and and_10 (and_10_out, not_3_out, dirty);
  and and_11 (and_11_out, not_1_out, St1, St0, CPU_Read);
  and and_12 (and_12_out, St2, not_3_out);
  or or_1 (St2_next, and_1_out, and_2_out, and_3_out);
  or or_2 (St1_next, and_4_out, and_5_out, and_6_out, and_7_out);
  or or_3 (St0_next, and_8_out, and_9_out, and_10_out, and_11_out, and_12_out);
endmodule

module getoutput (
  input  St2,
  input  St1,
  input  St0,
  output init,
  output ready,
  output mem_Read,
  output mem_Write,
  output update_Age,
  output ch_DidContain
);

  wire not_1_out, not_2_out, not_3_out;

  not not_1 (not_1_out, St2);
  not not_2 (not_2_out, St1);
  not not_3 (not_3_out, St0);
  and and_1 (init, not_1_out, not_2_out, not_3_out);
  and and_2 (ready, not_1_out, not_2_out, St0);
  and and_3 (mem_Read, St2, not_2_out, not_3_out);
  and and_4 (mem_Write, St2, not_2_out, St0);
  and and_5 (update_Age, not_1_out, St1, St0);
  and and_6 (ch_DidContain, not_1_out, St1, not_3_out);
endmodule
